# Fritzing sketch midi (saved by Fritzing 0.9.8b)
breadboards: 1

parts:
  SOM1 = Daisy Seed [chip_label=IC package="DIP (Dual Inline) [THT]"]
  Part1 = Audio Jack Breakout
  D1 = Schottky Diode [part_number=1N5817 package="300 mil [THT]"]
  R1 = Resistor [tolerance=±5% power=0.25 resistance=220 package=THT]
  IC1 = IC, DIP package, 6 pins [chip_label=H11L1]
  C1 = Ceramic Capacitor [capacitance=100nF voltage=35V package="100 mil [THT, multilayer]"]
  R2 = Resistor [tolerance=±5% power=0.25 resistance=470 package=THT]

nets:
  N1: SOM1.pin_15, IC1.pin4, R2.Pin_1
  N2: SOM1.pin_20, SOM1.pin_40, IC1.pin5, C1.1
  N3: SOM1.pin_21, R2.Pin_0
  N4: SOM1.pin_38, IC1.pin6, C1.0
  N5: Part1.RING_SHUNT, D1.cathode, R1.Pin_0
  N6: Part1.TIP, D1.anode, IC1.pin2
  N7: R1.Pin_1, IC1.pin1

notes:
  RSH and RNG are reversed on this image!

custom parts:
  Daisy Seed: Daisy is an embedded platform for music. It features everything you need for creating high fidelity audio hardware devices. Just plug in a USB cable and start making sound! No soldering required.
